# Fritzing sketch Infrequency (saved by Fritzing 0.9.2b)

parts:
  Part3 = Triple Axis Accelerometer Breakout - ADXL345
  Raspberry_Pi1 = Raspberry Pi B rev2

nets:
  GND: Part3.GND, Raspberry_Pi1.GND
  VCC: Part3.VCC, Part3.CS, Raspberry_Pi1.3V3
  N1: Part3.SDA, Raspberry_Pi1.GPIO_2
  N2: Part3.SCL, Raspberry_Pi1.GPIO_3
